// Logisim project ZAD1 - Bramki logiczne.circ as structural Verilog: 1 circuit, main circuit main
module main (
  input  a,
  input  b,
  input  c,
  input  d,
  output out_5
);

  wire nand_1_out, nand_2_out, nand_3_out, nand_4_out;

  nand nand_1 (nand_1_out, ~a, ~b, ~c);  // NAND_Gate
  nand nand_2 (nand_2_out, ~a, ~c, d);  // NAND_Gate
  nand nand_3 (nand_3_out, ~a, ~b, d);  // NAND_Gate
  nand nand_4 (nand_4_out, a, c, d);
  nand nand_5 (out_5, nand_1_out, nand_2_out, nand_3_out, nand_4_out);
endmodule
