// Logisim project ZAD2 - Robot.circ as structural Verilog: 1 circuit, main circuit main
module main (
  input  F,
  input  L,
  input  R,
  output WL,
  output WR
);

  wire nor_1_out, nor_2_out, nor_3_out;

  nor nor_1 (nor_1_out, ~F, L);  // NOR_Gate
  nor nor_2 (nor_2_out, ~F, ~R);  // NOR_Gate
  nor nor_3 (nor_3_out, ~F, ~L);  // NOR_Gate
  nor nor_4 (WL, nor_1_out, nor_2_out);
  nor nor_5 (WR, nor_3_out, nor_3_out);
endmodule
