// Logisim project ZAD3 - Układy sekwencyjne.circ as structural Verilog: 6 circuits, main circuit rejestr4bit
module rejestr4bit (
  input  wej,
  input  clr
);

  wire clock_1_out, d_ff_1_q, d_ff_2_q, d_ff_3_q, d_ff_4_q;

  Clock clock_1 (.out(clock_1_out));
  D_Flip_Flop d_ff_1 (.clk(clock_1_out), .D(wej), .Q(d_ff_1_q), .reset(clr));  // open: Qn, preset, en
  D_Flip_Flop d_ff_2 (.clk(clock_1_out), .D(d_ff_1_q), .Q(d_ff_2_q), .reset(clr));  // open: Qn, preset, en
  D_Flip_Flop d_ff_3 (.clk(clock_1_out), .D(d_ff_2_q), .Q(d_ff_3_q), .reset(clr));  // open: Qn, preset, en
  D_Flip_Flop d_ff_4 (.clk(clock_1_out), .D(d_ff_3_q), .Q(d_ff_4_q), .reset(clr));  // open: Qn, preset, en
  // Probe on d_ff_4_q
endmodule

module licznik3do9 (
);

  wire and_1_out, clock_1_out, d_ff_1_qn, d_ff_2_qn, d_ff_3_qn, d_ff_4_qn;
  wire [3:0] d_ff_1_q;

  Hex_Digit_Display hex_digit_display_1 (.value(d_ff_1_q));  // open: dp
  Clock clock_1 (.out(clock_1_out));
  D_Flip_Flop d_ff_1 (
    .clk(clock_1_out), .D(d_ff_1_qn), .Q(d_ff_1_q[0]), .Qn(d_ff_1_qn), .preset(and_1_out));  // open: en, reset
  and and_1 (and_1_out, d_ff_1_q[1], d_ff_1_q[3]);
  D_Flip_Flop d_ff_2 (
    .clk(d_ff_1_qn), .D(d_ff_2_qn), .Q(d_ff_1_q[1]), .Qn(d_ff_2_qn), .preset(and_1_out));  // open: en, reset
  D_Flip_Flop d_ff_3 (
    .clk(d_ff_2_qn), .D(d_ff_3_qn), .Q(d_ff_1_q[2]), .Qn(d_ff_3_qn), .reset(and_1_out));  // open: preset, en
  D_Flip_Flop d_ff_4 (
    .clk(d_ff_3_qn), .D(d_ff_4_qn), .Q(d_ff_1_q[3]), .Qn(d_ff_4_qn), .reset(and_1_out));  // open: preset, en
endmodule

module rng (
  input  clr
);

  wire clock_1_out, xor_1_out;
  wire [3:0] d_ff_1_q;

  Hex_Digit_Display hex_digit_display_1 (.value(d_ff_1_q));  // open: dp
  Clock clock_1 (.out(clock_1_out));
  D_Flip_Flop d_ff_1 (.clk(clock_1_out), .D(xor_1_out), .Q(d_ff_1_q[0]), .reset(clr));  // open: Qn, preset, en
  xor xor_1 (xor_1_out, d_ff_1_q[3], d_ff_1_q[2]);
  D_Flip_Flop d_ff_2 (.clk(clock_1_out), .D(d_ff_1_q[0]), .Q(d_ff_1_q[1]), .reset(clr));  // open: Qn, preset, en
  D_Flip_Flop d_ff_3 (.clk(clock_1_out), .D(d_ff_1_q[1]), .Q(d_ff_1_q[2]), .reset(clr));  // open: Qn, preset, en
  D_Flip_Flop d_ff_4 (.clk(clock_1_out), .D(d_ff_1_q[2]), .Q(d_ff_1_q[3]), .reset(clr));  // open: Qn, preset, en
endmodule

module RSlatch (
  input  wej,
  input  latch,
  output wyj
);

  wire nand_1_out, nand_2_out, nand_4_out;

  nand nand_1 (nand_1_out, wej, latch);
  nand nand_2 (nand_2_out, latch, ~wej);  // NAND_Gate
  nand nand_3 (wyj, nand_1_out, nand_4_out);
  nand nand_4 (nand_4_out, wyj, nand_2_out);
endmodule

module rejest_zatrzask (
  input  zatrzask,
  input  wej,
  input  clr
);

  wire clock_1_out, d_ff_1_q, d_ff_2_q, d_ff_3_q, d_ff_4_q;
  wire [3:0] rslatch_1_wyj;

  Clock clock_1 (.out(clock_1_out));
  Hex_Digit_Display hex_digit_display_1 (.value(rslatch_1_wyj));  // open: dp
  RSlatch rslatch_1 (.wej(d_ff_1_q), .latch(zatrzask), .wyj(rslatch_1_wyj[0]));
  D_Flip_Flop d_ff_1 (.clk(clock_1_out), .D(wej), .Q(d_ff_1_q), .reset(clr));  // open: Qn, preset, en
  RSlatch rslatch_2 (.wej(d_ff_2_q), .latch(zatrzask), .wyj(rslatch_1_wyj[1]));
  D_Flip_Flop d_ff_2 (.clk(clock_1_out), .D(d_ff_1_q), .Q(d_ff_2_q), .reset(clr));  // open: Qn, preset, en
  RSlatch rslatch_3 (.wej(d_ff_3_q), .latch(zatrzask), .wyj(rslatch_1_wyj[2]));
  D_Flip_Flop d_ff_3 (.clk(clock_1_out), .D(d_ff_2_q), .Q(d_ff_3_q), .reset(clr));  // open: Qn, preset, en
  D_Flip_Flop d_ff_4 (.clk(clock_1_out), .D(d_ff_3_q), .Q(d_ff_4_q), .reset(clr));  // open: Qn, preset, en
  RSlatch rslatch_4 (.wej(d_ff_4_q), .latch(zatrzask), .wyj(rslatch_1_wyj[3]));
  // Probe on d_ff_4_q
endmodule

module sygnalizacja (
  input  x
);

  wire and_1_out, and_2_out, clock_1_out, or_1_out, Q0_q, Q1_q, Q1_qn, xor_1_out;

  Clock clock_1 (.out(clock_1_out));
  or or_1 (or_1_out, Q0_q, ~x);  // OR_Gate
  and and_1 (and_1_out, x, ~Q1_q);  // AND_Gate
  D_Flip_Flop Q1 (.clk(clock_1_out), .D(or_1_out), .Q(Q1_q), .Qn(Q1_qn));  // open: preset, en, reset
  D_Flip_Flop Q0 (.clk(clock_1_out), .D(and_1_out), .Q(Q0_q));  // open: Qn, preset, en, reset
  LED led_1 (.in(Q1_qn));
  LED led_2 (.in(xor_1_out));
  xor xor_1 (xor_1_out, Q1_q, Q0_q);
  and and_2 (and_2_out, Q1_q, Q0_q);
  LED led_3 (.in(and_2_out));
endmodule
